# Fritzing sketch wiring (saved by Fritzing 0.9.3b)

parts:
  ProMini_3_3v = Arduino Pro Mini (3.3V)
  Float_switch = Round Pushbutton
  2_x_AA = Battery
  part = DS18B20 1-Wire Temperature Sensor
  R1 = Resistor [tolerance=±5% resistance=4.7k package=THT]
  R2 = Resistor [tolerance=±5% resistance=1M package=THT]
  NRF24L01 = NRF24L01+ Breakout Board
  StepUp_3_3v = NCP1400 Step-Up Breakout
  R3 = Resistor [tolerance=±5% resistance=470k package=THT]
  C1 = Ceramic Capacitor [capacitance=100nF package="200 mil [THT, multilayer]"]
  US100 = US-100 Ultrasonic Rangefinder

nets:
  3.3V: ProMini_3_3v.VCC, part.VDD, R1.Pin_0, StepUp_3_3v.VOUT
  GND: ProMini_3_3v.GND, Float_switch.leg0, 2_x_AA.-, part.GND, NRF24L01.GND, StepUp_3_3v.GND, R3.Pin_1, C1.0, US100.GND*
  N1: ProMini_3_3v.A4, US100.VCC
  N2: ProMini_3_3v.A0, R2.Pin_1, R3.Pin_0, C1.1
  N3: ProMini_3_3v.SCK, NRF24L01.SCK
  N4: ProMini_3_3v.MISO, NRF24L01.MOSI
  N5: ProMini_3_3v.MOSI, NRF24L01.MISO
  N6: ProMini_3_3v.D10, NRF24L01.CS
  N7: ProMini_3_3v.D9, NRF24L01.CE
  N8: ProMini_3_3v.D6, US100.Trig/Tx
  N9: ProMini_3_3v.D5, US100.Echo/Rx
  N10: ProMini_3_3v.D3, part.DQ, R1.Pin_1
  N11: ProMini_3_3v.D2, Float_switch.leg1
  VCC: 2_x_AA.+, R2.Pin_0, NRF24L01.VCC, StepUp_3_3v.VIN
